# Fritzing sketch принципиальная схема (saved by Fritzing 0.9.4)
# 18650 Li-ion Battery: CC-BY Dr Kristofer Chan, King's College London/Remote-research.org

parts:
  Компонент1 = Arduino Uno (Rev3) - ICSP
  BAT1 = 18650 Li-ion Battery [package=battery-18650]
  BAT2 = 18650 Li-ion Battery [package=battery-18650]
  TP1 = TP4056 [chip_label=TP4056 package="DIP (Dual Inline) [THT]"]
  D1 = SOLAR-IXYS [package=solarbit-12x1]
  R7 = PHOTOCELL [package=photocell]
  R8 = Resistor [tolerance=±5% resistance=10k package="0603 [SMD]"]
  R11 = PHOTOCELL [package=photocell]
  R12 = Resistor [tolerance=±5% resistance=10k package="0603 [SMD]"]
  JP1 = Header 3 [package=screwterminal-3.5mm-3_lock.007s]
  JP2 = Header 3 [package=screwterminal-3.5mm-3_lock.007s]
  J1 = Basic Servo

nets:
  N1: Компонент1.A0, R11.P$2, R12.Pin_1
  N2: Компонент1.A1, R7.P$2, R8.Pin_1
  5V: Компонент1.5V, J1.vcc
  N3: Компонент1.D9_PWM, J1.pulse
  GND: Компонент1.GND, TP1.pin6, JP1.3, J1.gnd
  N4: Компонент1.3V3, JP2.3
  N5: Компонент1.VIN, TP1.pin3
  N6: BAT1.-, BAT2.-, TP1.pin5
  N7: BAT1.+, BAT2.+, TP1.pin4
  N8: TP1.pin1, D1.A
  N9: TP1.pin2, D1.C
  N10: R7.P$1, JP2.1
  N11: R8.Pin_0, JP1.1
  N12: R11.P$1, JP2.2
  N13: R12.Pin_0, JP1.2

notes:
  солнечная панель
  Аккумуляторная сборка
  18650 1s2p
  4400mAh 3.7-4.2v
  TP4057
  Контроллер заряда-разряда Li-Ion 1s
  MG90s 180 сервопривод - обеспечивает поворот солнечной панели
  Отладочная плата Arduino Uno R3
  Датчики освещенности на базе фоторезисторов на делителе напряжения
  Питание 3.3v для пониженного электропотребления
  клеммы питания

custom parts:
  18650 Li-ion Battery: 18650 li-ion Battery Standard 18650 battery with interactive connectors Creative Common Attribution 4.0 International (CC-BY 4.0) license. Any use of this part requires attribution of Dr Kristofer Chan, Department of Geography, King's College London. Contact kristofer.chan [at] kcl.ac.uk OR kris [at] remote-research.org for further information.
  TP4056: A DIP stand-in part for whatever IC you want. With 6 pins on a 300mil dual inline package (DIP) footprint.
